# Fritzing sketch uno (saved by Fritzing 0.9.3b)
breadboards: 1

parts:
  부품1 = Arduino Uno (Rev3)
  L1 = Solenoid
  부품2 = Bluetooth HC-05 Macho

nets:
  N1: 부품1.D2, 부품2.TXD
  N2: 부품1.D3_PWM, 부품2.RXD
  N3: 부품1.D4, L1.pin2
  N4: 부품1.D5_PWM, 부품2.State
  5V: 부품1.5V, 부품2.VCC
  GND: 부품1.GND, L1.pin1, 부품2.GND

// code stored in the sketch: BTSetup.ino
#include <SoftwareSerial.h>

SoftwareSerial bluetooth(2, 3); //BlueTooth(Rx, Tx)

void setup() {
  Serial.begin(9600);
  bluetooth.begin(9600);
}

void loop() {
  if (bluetooth.available()){
    Serial.write(bluetooth.read());
  }
  if (Serial.available()){
    bluetooth.write(Serial.read());
  }
}
